# Fritzing sketch arduino circuit (saved by Fritzing 0.9.6b)
breadboards: 1

parts:
  Part1 = Adafruit Feather 32u4 RFM9xW LoRa [part_number="Adafruit #3078 and Adafruit #3079"]
  R1 = Resistor [tolerance=±5% power=0.25 resistance=100000 package=THT]
  R2 = Resistor [tolerance=±5% power=0.25 resistance=100000 package=THT]
  DS1 = DS18B20 1-Wire Temperature Sensor [part_number=DS18B20]
  R3 = Resistor [tolerance=±5% power=0.25 resistance=100000 package=THT]
  C1 = Electrolytic Capacitor [capacitance=1µF voltage=35V package="100 mil [THT, electrolytic]"]
  C2 = Electrolytic Capacitor [capacitance=1µF voltage=35V package="100 mil [THT, electrolytic]"]
  C3 = Electrolytic Capacitor [capacitance=1µF voltage=35V package="100 mil [THT, electrolytic]"]
  J1 = Basic Servo

nets:
  N1: Part1.A4, R1.Pin_1, R2.Pin_0
  GND: Part1.GND, R2.Pin_1, DS1.GND, C1.-, C2.-, C3.-, J1.gnd
  +3V3: Part1.+3V3, DS1.VDD, R3.Pin_1, C1.+, C2.+, C3.+, J1.vcc
  N2: Part1.VBAT, R1.Pin_0
  N3: Part1.11, J1.pulse
  N4: Part1.10, DS1.DQ, R3.Pin_0

custom parts:
  Adafruit Feather 32u4 RFM9xW LoRa: This is the Adafruit Feather 32u4 LoRa Radio (RFM9x) - our take on an microcontroller with a "Long Range (LoRa)" packet radio transceiver with built in USB and battery charging. Its an Adafruit Feather 32u4 with a 868/915 MHz radio module cooked in! Great for making wireless networks that can go further than 2.4GHz 802.15.4 and similar, are more flexible than Bluetooth LE and without the high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
