# Fritzing sketch raspberry pi circuit (saved by Fritzing 0.9.6b)
breadboards: 1

parts:
  Mod1 = Raspberry Pi 4B
  Part1 = Adafruit T-Cobbler Plus [part_number="Adafruit #1989 and #2028"]
  Part2 = Adafruit RFM9x LoRa Radio [part_number="Adafruit #3072 and #3073"]
  DS1 = DS18B20 1-Wire Temperature Sensor [part_number=DS18B20]
  R1 = Resistor [tolerance=±5% power=0.25 resistance=4700 package=THT]
  ANT1 = Antenna

nets:
  N1: Mod1.GND, Mod1.GPIO5, Mod1.GPIO13, Mod1.GPIO21
  N2: Mod1.ID_SD, Mod1.ID_SC
  N3: Mod1.GPIO6, Mod1.GPIO12
  N4: Mod1.GPIO19, Mod1.GPIO16
  N5: Mod1.GPIO26, Mod1.GPIO20
  +3.3V: Part1.+3.3V, Part2.VIN, DS1.VDD, R1.Pin_1
  N6: Part1.GPIO4, DS1.DQ, R1.Pin_0
  GND: Part1.GND, Part2.GND, DS1.GND
  N7: Part1.MOSI, Part2.MOSI
  N8: Part1.MISO, Part2.MISO
  N9: Part1.SCLK, Part2.SCK
  N10: Part1.GPIO5, Part2.DIO0
  N11: Part1.GPIO25, Part2.RST
  N12: Part1.CE1, Part2.CS
  N13: Part2.ANTENNA, ANT1.antenna_lead

custom parts:
  Adafruit T-Cobbler Plus: The Raspberry Pi has landed on the Maker World like a 40-GPIO pinned, quad-USB ported, credit card sized bomb of DIY joy. And while you can use most of our great Model B accessories by hooking up our downgrade cable, its probably a good time to upgrade your set up and accessorize using all of the 40 pins. That's why we now carry the Assembled Adafruit Pi T-Cobbler Plus - Breakout + Cable for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
  Adafruit RFM9x LoRa Radio: Sending data over long distances is like magic, and now you can be a magician with this range of powerful and easy-to-use radio modules. Sure, sometimes you want to talk to a computer (a good time to use WiFi) or perhaps communicate with a Phone (choose Bluetooth Low Energy!) but what if you want to send data very far? Most WiFi, Bluetooth, Zigbee and other wireless chipsets use 2.4GHz, which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
